# Fritzing sketch Schaltplan (saved by Fritzing 0.9.3b)
breadboards: 2

parts:
  Bauteil1 = Arduino Uno (Rev3)
  LED1 = LED - 5mm [color="Red (633nm)" package="5 mm [THT]"]
  LED2 = LED - 5mm [color="Red (633nm)" package="5 mm [THT]"]
  LED3 = LED - 5mm [color="Red (633nm)" package="5 mm [THT]"]
  LED4 = LED - 5mm [color="Red (633nm)" package="5 mm [THT]"]
  U4 = POT [package=alps_pot]
  S2 = Pushbutton [package="[SMD]"]
  S3 = Pushbutton [package="[SMD]"]
  S4 = Pushbutton [package="[SMD]"]
  S5 = Pushbutton [package="[SMD]"]
  R9 = Resistor [tolerance=±5% resistance=220 package=THT]
  R10 = Resistor [tolerance=±5% resistance=220 package=THT]
  R11 = Resistor [tolerance=±5% resistance=220 package=THT]
  R12 = Resistor [tolerance=±5% resistance=220 package=THT]
  J1 = Piezo Speaker
  Bauteil2 = LCD1602-I2C

nets:
  N1: Bauteil1.D8, S4.Pin_3, S4.Pin_4, R9.Pin_1
  N2: Bauteil1.D9_PWM, LED4.anode
  N3: Bauteil1.D10_PWM/SS, J1.pin2
  N4: Bauteil1.A4/SDA, Bauteil2.SDA
  N5: Bauteil1.A5/SCL, Bauteil2.SCL
  N6: Bauteil1.D2, S2.Pin_3, S2.Pin_4, R11.Pin_1
  N7: Bauteil1.D3_PWM, LED1.anode
  N8: Bauteil1.D4, S5.Pin_3, S5.Pin_4, R10.Pin_1
  N9: Bauteil1.D5_PWM, LED2.anode
  N10: Bauteil1.D6_PWM, S3.Pin_3, S3.Pin_4, R12.Pin_1
  N11: Bauteil1.D7, LED3.anode
  5V: Bauteil1.5V, S2.Pin_1, S2.Pin_2, S3.Pin_1, S3.Pin_2, S4.Pin_1, S4.Pin_2, S5.Pin_1, S5.Pin_2, R9.Pin_0, R10.Pin_0, R11.Pin_0, R12.Pin_0, J1.pin1, Bauteil2.VCC
  GND: Bauteil1.GND, U4.E, Bauteil2.GND
  N12: LED1.cathode, LED2.cathode, LED3.cathode, LED4.cathode, U4.S

custom parts:
  LCD1602-I2C: A standard character display, usually with 2x16 characters. Comes in many colors with LCM1602 IIC attached.
